// Logisim project 3 Bit Binary Counter using T Flip Flop.circ as structural Verilog: 1 circuit, main circuit main
module main (
  output A0,
  output A1,
  output A2
);

  wire and_1_out, clock_1_out;

  Clock clock_1 (.out(clock_1_out));
  T_Flip_Flop t_ff_1 (.clk(clock_1_out), .T(1'b1), .Q(A0));  // open: Qn, preset, reset, en
  T_Flip_Flop t_ff_2 (.clk(clock_1_out), .T(A0), .Q(A1));  // open: Qn, preset, reset, en
  T_Flip_Flop t_ff_3 (.clk(clock_1_out), .T(and_1_out), .Q(A2));  // open: Qn, preset, reset, en
  and and_1 (and_1_out, A0, A1);
endmodule
