// Logisim project Clocked RS Flip Flop.circ as structural Verilog: 1 circuit, main circuit main
module main (
  input  R,
  input  S,
  output Q,
  output Q_prime
);

  wire and_1_out, and_2_out, CP_out;

  Clock CP (.out(CP_out));
  and and_1 (and_1_out, R, CP_out);
  and and_2 (and_2_out, CP_out, S);
  nor nor_1 (Q, and_1_out, Q_prime);
  nor nor_2 (Q_prime, Q, and_2_out);
endmodule
