// Logisim project DEMUX.circ as structural Verilog: 1 circuit, main circuit main
module main (
  input  E,
  input  A,
  input  B,
  output out_4,
  output out_5,
  output out_6,
  output out_7
);

  wire undriven;
  wire [1:0] undriven_2;

  Demultiplexer #(.select(2)) demultiplexer_1 (
    .out0(out_4), .out1(out_5), .out2(out_6), .out3(out_7), .in(E), .sel(undriven_2), .en(undriven));
endmodule
