// Logisim project Full Adder using Decoder.circ as structural Verilog: 1 circuit, main circuit main
module main (
  input  z,
  input  y,
  input  x,
  output S,
  output C
);

  wire and_1_out, and_2_out, and_3_out, and_4_out, and_5_out, and_6_out, and_7_out, and_8_out, not_1_out,
       not_2_out, not_3_out;

  not not_1 (not_1_out, z);
  not not_2 (not_2_out, y);
  not not_3 (not_3_out, x);
  and and_1 (and_1_out, not_1_out, not_2_out, not_3_out);
  and and_2 (and_2_out, z, not_2_out, not_3_out);
  and and_3 (and_3_out, not_1_out, y, not_3_out);
  and and_4 (and_4_out, z, y, not_3_out);
  and and_5 (and_5_out, not_1_out, not_2_out, x);
  and and_6 (and_6_out, z, not_2_out, x);
  and and_7 (and_7_out, not_1_out, y, x);
  and and_8 (and_8_out, z, y, x);
  or or_1 (S, and_2_out, and_3_out, and_5_out, and_8_out);
  or or_2 (C, and_4_out, and_6_out, and_7_out, and_8_out);
endmodule
