// Logisim project Full Adder.circ as structural Verilog: 1 circuit, main circuit main
module main (
  input  x,
  input  y,
  input  z,
  output Sum____x_XOR_y_XOR_z,
  output Carry___xy___yz___zx
);

  wire and_1_out, and_2_out, and_3_out, xor_1_out;

  xor xor_1 (xor_1_out, x, y);
  and and_1 (and_1_out, x, y);
  and and_2 (and_2_out, y, z);
  and and_3 (and_3_out, z, x);
  xor xor_2 (Sum____x_XOR_y_XOR_z, xor_1_out, z);
  or or_1 (Carry___xy___yz___zx, and_1_out, and_2_out, and_3_out);
endmodule
