// Logisim project Full Subtractor.circ as structural Verilog: 1 circuit, main circuit main
module main (
  input  x,
  input  y,
  input  z,
  output Difference____x_XOR_y_XOR_z,
  output Borrow___x_prime_y___x_prime_z___yz
);

  wire and_1_out, and_2_out, and_3_out, not_1_out, xor_1_out;

  xor xor_1 (xor_1_out, x, y);
  not not_1 (not_1_out, x);
  xor xor_2 (Difference____x_XOR_y_XOR_z, xor_1_out, z);
  and and_1 (and_1_out, not_1_out, y);
  and and_2 (and_2_out, not_1_out, z);
  and and_3 (and_3_out, z, y);
  or or_1 (Borrow___x_prime_y___x_prime_z___yz, and_1_out, and_2_out, and_3_out);
endmodule
