// Logisim project Half Adder.circ as structural Verilog: 1 circuit, main circuit main
module main (
  input  x,
  input  y,
  output Sum___x_XOR_y,
  output Carry___X_Y
);

  xor xor_1 (Sum___x_XOR_y, x, y);
  and and_1 (Carry___X_Y, x, y);
endmodule
