// Logisim project Half Subtractor.circ as structural Verilog: 1 circuit, main circuit main
module main (
  input  x,
  input  y,
  output Difference___x_XOR_y,
  output Borrow___x_prime_y
);

  wire not_1_out;

  not not_1 (not_1_out, x);
  xor xor_1 (Difference___x_XOR_y, x, y);
  and and_1 (Borrow___x_prime_y, not_1_out, y);
endmodule
