// Logisim project MUX.circ as structural Verilog: 1 circuit, main circuit main
module main (
  input  _0,
  input  _1,
  input  _2,
  input  _3,
  input  s1,
  input  s0,
  output Output
);

  wire undriven_2;
  wire [1:0] undriven;

  Multiplexer #(.select(2)) multiplexer_1 (
    .in0(_0), .in1(_1), .in2(_2), .in3(_3), .out(Output), .sel(undriven), .en(undriven_2));
endmodule
