// Logisim project SR Latch(with NAND).circ as structural Verilog: 1 circuit, main circuit main
module main (
  input  Set,
  input  Reset,
  output Q,
  output Q_prime
);

  nand nand_1 (Q, Set, Q_prime);
  nand nand_2 (Q_prime, Q, Reset);
endmodule
