// Logisim project untitled bcd.circ as structural Verilog: 1 circuit, main circuit main
module main (
  input  w,
  input  x,
  input  y,
  input  z,
  output out_5
);

  wire not_1_out, not_2_out, not_3_out, not_4_out;

  not not_1 (not_1_out, w);
  not not_2 (not_2_out, x);
  not not_3 (not_3_out, y);
  not not_4 (not_4_out, z);
  and and_1 (out_5, not_1_out, not_4_out);
  // AND_Gate and_2 has open pins: in0=not_3_out, out=open
  // AND_Gate and_3 is placed but not wired
  // AND_Gate and_4 is placed but not wired
  // AND_Gate and_5 is placed but not wired
  // AND_Gate and_6 is placed but not wired
  // AND_Gate and_7 is placed but not wired
  // AND_Gate and_8 is placed but not wired
  // AND_Gate and_9 is placed but not wired
endmodule
